# Fritzing sketch main (saved by Fritzing 0.9.2b)
breadboards: 1

parts:
  Raspberry_Pi1 = Raspberry Pi 2
  Part1 = Barometric Pressure Sensor - BMP085 Breakout

nets:
  3V3: Raspberry_Pi1.3V3, Part1.Vcc
  GND: Raspberry_Pi1.GND, Part1.GND
  N1: Raspberry_Pi1.GPIO15, Part1.RXD
  N2: Raspberry_Pi1.GPIO14, Part1.TXD

custom parts:
  Barometric Pressure Sensor - BMP085 Breakout: Description: This is a simple breakout board for the BMP085 high-precision, low-power barometric pressure sensor. The BMP085 offers a measuring range of 300 to 1100 hPa with an absolute accuracy of down to 0.03 hPa. It's based on piezo-resistive technology for EMC robustness, high accuracy and linearity as well as long term stability. This sensor supports a voltage supply between 1.8 and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
