# Fritzing sketch mm_roaming (saved by Fritzing 0.9.2b)

parts:
  Raspberry_Pi_Zero1 = Raspberry Pi Zero
  GY-NEO6MV3 = SUP500F [package=sup500f]
  U1 = LIPO-2000mAh [package=lipo-2000]  # not connected
  InAir4 = InAir4
  PiScreen = PiScreen_1 [package=2x10_lock]
  U2 = PiScreen_2 [package=2x10_lock]
  Part1 = Power Cell LiPo Charger/Booster  # not connected

nets:
  N1: Raspberry_Pi_Zero1.3v3, GY-NEO6MV3.TX-O, PiScreen.1_(3.3V)
  N2: Raspberry_Pi_Zero1.GPIO2, PiScreen.3_()
  N3: Raspberry_Pi_Zero1.GPIO3, PiScreen.5_(SCL)
  N4: Raspberry_Pi_Zero1.GIPO4, InAir4.VS
  N5: Raspberry_Pi_Zero1.GND, GY-NEO6MV3.RX-I, PiScreen.11_(TP_INT)
  N6: Raspberry_Pi_Zero1.GIPO22, PiScreen.15_(BACKLIGHT)
  N7: Raspberry_Pi_Zero1.GIPO10, InAir4.SI, PiScreen.19_(LCD_SI_/_TP_SI)
  N8: Raspberry_Pi_Zero1.GIPO9, InAir4.SO, U2.21_(TP_SO)
  N9: Raspberry_Pi_Zero1.GIPO11, InAir4.CK
  N10: Raspberry_Pi_Zero1.GIPO5, InAir4.D2
  N11: Raspberry_Pi_Zero1.GIPO6, InAir4.D3
  N12: Raspberry_Pi_Zero1.GIPO13, InAir4.D0
  N13: Raspberry_Pi_Zero1.GIPO7, InAir4.CS
  N14: Raspberry_Pi_Zero1.GIPO8, U2.24_(LCD_CS)
  N15: Raspberry_Pi_Zero1.GIPO25, U2.22_(RST)
  N16: Raspberry_Pi_Zero1.GIPO24, PiScreen.18_(LCD_RS)
  N17: Raspberry_Pi_Zero1.GIPO23, InAir4.D1
  N18: Raspberry_Pi_Zero1.GIPO15, GY-NEO6MV3.VCC
  N19: Raspberry_Pi_Zero1.GIPO14, GY-NEO6MV3.GND

notes:
  GND: Black
  VCC: Red (3.3v)
  RX: Yellow
  TX: Green
  3.3V
  GND
  5V
  NC. Will be conected after modified device overlay is used to open more chip select pins

custom parts:
  PiScreen_1: This was SPECIALLY designed to be used with our Graphic LCD Backpack. Be sure you want to use this! It is not only staggered on each line of header holes, but IT IS ALSO offset of the center point of the top and bottom lines by 5 mil. This causes the headers to lock into place on the standard footprint on the LCD screen. The extra squares on the tdocu layer are there simply to reference other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
  PiScreen_2: This was SPECIALLY designed to be used with our Graphic LCD Backpack. Be sure you want to use this! It is not only staggered on each line of header holes, but IT IS ALSO offset of the center point of the top and bottom lines by 5 mil. This causes the headers to lock into place on the standard footprint on the LCD screen. The extra squares on the tdocu layer are there simply to reference other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
